# Fritzing sketch Robot (saved by Fritzing 0.9.1b)
breadboards: 1
perfboards: 1

parts:
  Part1 = HC-SR04 Ultrasonic Rangemeter
  M1 = DC Motor
  M2 = DC Motor
  LM35_TempSensor1 = LM35 TempSensor
  VCC1 = 4 x AAA Battery Mount
  Part2 = Arduino Uno (Rev3)
  Part3 = 2A MOTOR SHIELD 9
  U1 = SWITCH_SPDT [package=kps-1290]
  Part6 = Bluetooth HC-05 Macho
  RE1 = Rotary Encoder [package=THT]
  Part8 = Arduino Prototyping Shield
  R2 = Resistor [tolerance=±5% resistance=2.0k package=THT]
  R3 = Resistor [tolerance=±5% resistance=1k package=THT]
  RE4 = Rotary Encoder [package=THT]
  JP7 = Header 1 [package=1x01_offset]
  JP12 = Header 1 [package=1x01_offset]
  C1 = Ceramic Capacitor [capacitance=100nF package="100 mil [THT, multilayer]"]
  C2 = Ceramic Capacitor [capacitance=100nF package="100 mil [THT, multilayer]"]
  R4 = Resistor [tolerance=±5% resistance=10k package=THT]
  C5 = Tantalum Capacitor [capacitance=1μF package="100 mil [THT, tantalum]"]
  LCD1 = LCD screen

nets:
  N1: Part1.VCC, Part8.N$84
  N2: Part1.Trig, Part8.D8
  N3: Part1.Echo, Part8.A3
  N4: Part1.GND, Part8.N$76
  N5: M1.pin_1, Part3.M1+, C1.1
  N6: M1.pin_2, Part3.M1-, C1.0
  N7: M2.pin_1, Part3.M2+, C2.1
  N8: M2.pin_2, Part3.M2-, C2.0
  N9: LM35_TempSensor1.POWER, Part8.N$332
  N10: LM35_TempSensor1.GND, Part8.A0
  N11: LM35_TempSensor1.INPUT, Part8.N$27
  N12: VCC1.-, Part3.GND#0
  N13: VCC1.+, U1.O
  N14: Part2.A0, Part3.A0
  N15: Part2.A1, Part3.A1
  N16: Part2.A2, Part3.A2
  N17: Part2.A3, Part3.A3
  N18: Part2.A4/SDA, Part3.A4
  N19: Part2.A5/SCL, Part3.A5
  N20: Part2.D8, Part3.D8
  N21: Part2.D9_PWM, Part3.D9
  N22: Part2.D10_PWM/SS, Part3.D10
  N23: Part2.D11_PWM/MOSI, Part3.D11
  N24: Part2.D12/MISO, Part3.D12
  N25: Part2.D13/SCK, Part3.D13
  N26: Part2.GND, Part3.GND#connector1pad-0-1-1-48-61, Part3.GND#connector1pad-0-1-9-9-4-9, Part3.GND#connector1pad-4-5-0-39-8-14
  N27: Part2.AREF, Part3.AFER
  N28: Part2.D1/TX, Part3.D1
  N29: Part2.D2, Part3.D2
  N30: Part2.D3_PWM, Part3.D3
  N31: Part2.D4, Part3.D4
  N32: Part2.D5_PWM, Part3.D5
  N33: Part2.D6_PWM, Part3.D6
  N34: Part2.D7, Part3.D7
  N35: Part2.RESET, Part3.RST
  3V3: Part2.3V3, Part3.3V3
  5V: Part2.5V, Part3.5V
  VIN: Part2.VIN, Part3.VIN
  N36: Part3.D0, U1.P
  N37: Part6.TXD, Part8.D0(RX)
  N38: Part6.RXD, R2.Pin_1, R3.Pin_0
  N39: Part6.VCC, Part8.N$178
  N40: Part6.GND, Part8.N$53, Part8.N$118, R2.Pin_0
  N41: RE1.EncoderPinA, Part8.N$77
  N42: RE1.EncoderPinC, Part8.N$67
  N43: RE1.EncoderPinB, Part8.N$177
  N44: Part8.D1(TX), R3.Pin_1
  N45: Part8.D2, Part8.N$410, JP7.1
  N46: Part8.D11, Part8.N$165, JP12.1
  N47: Part8.N$16, RE4.EncoderPinA
  N48: Part8.N$26, C5.+
  N49: Part8.N$37, RE4.EncoderPinB
  N50: Part8.N$41, RE4.EncoderPinC
  N51: Part8.N$304, C5.-
  N52: Part8.N$311, R4.Pin_0
  N53: Part8.N$400, R4.Pin_1
  VSS: LCD1.VSS, LCD1.VDD, LCD1.V0
  N54: LCD1.RS, LCD1.R/W, LCD1.E
  N55: LCD1.DB4, LCD1.DB5, LCD1.DB6
  N56: LCD1.DB7, LCD1.LED+, LCD1.LED-

notes:
  Encoder #2 to help wheels turn at the same rate so the robot goes straight
  Encoder #1 to help wheels turn at the same rate so the robot goes straight
  HC-05 Bluetooth for wireless communication between gyroscopic controller and robot
  Prototyping shield is detached from the motor shield to help display wiring
  LM35 Temperature Sensor
  LCD with I2C interface, represented by the perfboard
